// Logisim project 2 2 0 7 1 1 1-COUNTER.circ as structural Verilog: 2 circuits, main circuit main
module main (
  input  in_1
);

  wire and_1_out, and_2_out, and_3_out, and_4_out, and_5_out, and_6_out, and_7_out, clock_1_out,
       n7seg_1_out_5, n7seg_1_out_6, n7seg_1_out_7, n7seg_1_out_8, n7seg_1_out_9, n7seg_1_out_10,
       n7seg_1_out_11, not_1_out, not_2_out, not_3_out, not_4_out, not_5_out, not_6_out, not_7_out,
       not_8_out, not_9_out, or_1_out, or_2_out, or_3_out, or_4_out, or_5_out, t_ff_1_q, t_ff_2_q, t_ff_3_q,
       t_ff_4_q, t_ff_5_q;

  Clock clock_1 (.out(clock_1_out));
  or or_1 (or_1_out, t_ff_1_q, and_1_out);
  and and_1 (and_1_out, t_ff_2_q, not_1_out);
  not not_1 (not_1_out, t_ff_4_q);
  or or_2 (or_2_out, t_ff_3_q, t_ff_1_q, and_2_out, and_3_out);
  T_Flip_Flop t_ff_1 (.clk(clock_1_out), .T(or_1_out), .Q(t_ff_1_q));  // open: Qn, preset, reset, en
  LED led_1 (.in(t_ff_1_q));
  and and_2 (and_2_out, not_2_out, not_3_out);
  not not_2 (not_2_out, t_ff_4_q);
  not not_3 (not_3_out, t_ff_5_q);
  and and_3 (and_3_out, not_3_out, t_ff_2_q);
  T_Flip_Flop t_ff_2 (.clk(clock_1_out), .T(and_5_out), .Q(t_ff_2_q));  // open: Qn, preset, reset, en
  LED led_2 (.in(t_ff_2_q));
  or or_3 (or_3_out, and_4_out, t_ff_4_q);
  and and_4 (and_4_out, t_ff_5_q, not_4_out);
  not not_4 (not_4_out, t_ff_1_q);
  not not_5 (not_5_out, t_ff_3_q);
  T_Flip_Flop t_ff_3 (.clk(clock_1_out), .T(or_4_out), .Q(t_ff_3_q));  // open: Qn, preset, reset, en
  and and_5 (and_5_out, or_3_out, not_5_out);
  LED led_3 (.in(t_ff_3_q));
  not not_6 (not_6_out, t_ff_4_q);
  not not_7 (not_7_out, t_ff_5_q);
  T_Flip_Flop t_ff_4 (.clk(clock_1_out), .T(or_2_out), .Q(t_ff_4_q));  // open: Qn, preset, reset, en
  LED led_4 (.in(t_ff_4_q));
  and and_6 (and_6_out, not_6_out, not_7_out);
  not not_8 (not_8_out, t_ff_4_q);
  not not_9 (not_9_out, t_ff_5_q);
  or or_4 (or_4_out, and_6_out, t_ff_3_q);
  and and_7 (and_7_out, not_8_out, not_9_out);
  T_Flip_Flop t_ff_5 (.clk(clock_1_out), .T(or_5_out), .Q(t_ff_5_q));  // open: Qn, preset, reset, en
  LED led_5 (.in(t_ff_5_q));
  or or_5 (or_5_out, and_7_out, t_ff_1_q);
  _7seg u_7seg_1 (
    .in_1(in_1), .in_2(t_ff_3_q), .in_3(t_ff_4_q), .in_4(t_ff_5_q), .out_5(n7seg_1_out_5),
    .out_6(n7seg_1_out_6), .out_7(n7seg_1_out_7), .out_8(n7seg_1_out_8), .out_9(n7seg_1_out_9),
    .out_10(n7seg_1_out_10), .out_11(n7seg_1_out_11));
  _7_Segment_Display u_7_segment_display_1 (
    .g(n7seg_1_out_11), .f(n7seg_1_out_10), .a(n7seg_1_out_5), .b(n7seg_1_out_6), .e(n7seg_1_out_9),
    .d(n7seg_1_out_8), .c(n7seg_1_out_7));  // open: dp

  // Notes on the sheet:
  //   2207111
endmodule

module _7seg (
  input  in_1,
  input  in_2,
  input  in_3,
  input  in_4,
  output out_5,
  output out_6,
  output out_7,
  output out_8,
  output out_9,
  output out_10,
  output out_11
);

  wire and_1_out, and_2_out, and_3_out, and_4_out, and_5_out, and_6_out, and_7_out, and_8_out, and_9_out,
       and_10_out, and_11_out, and_12_out, and_13_out, and_14_out, and_15_out, and_16_out, and_17_out,
       not_1_out, not_2_out, not_3_out, not_4_out, not_5_out, not_6_out, not_7_out, not_8_out, not_9_out,
       not_10_out, not_11_out, not_12_out, not_13_out, not_14_out, not_15_out, not_16_out, not_17_out,
       not_18_out, not_19_out, not_20_out, not_21_out, or_1_out, or_5_out, or_7_out, or_8_out, or_9_out,
       or_10_out, or_11_out, or_12_out;

  not not_1 (not_1_out, in_2);
  not not_2 (not_2_out, in_4);
  not not_3 (not_3_out, in_3);
  not not_4 (not_4_out, in_4);
  not not_5 (not_5_out, in_3);
  not not_6 (not_6_out, in_2);
  not not_7 (not_7_out, in_4);
  not not_8 (not_8_out, in_2);
  not not_9 (not_9_out, in_3);
  not not_10 (not_10_out, in_2);
  not not_11 (not_11_out, in_4);
  not not_12 (not_12_out, in_4);
  not not_13 (not_13_out, in_3);
  not not_14 (not_14_out, in_4);
  not not_15 (not_15_out, in_3);
  not not_16 (not_16_out, in_4);
  not not_17 (not_17_out, in_2);
  not not_18 (not_18_out, in_3);
  not not_19 (not_19_out, in_4);
  and and_1 (and_1_out, not_1_out, not_2_out);
  and and_2 (and_2_out, in_2, in_4);
  not not_20 (not_20_out, in_2);
  and and_3 (and_3_out, not_3_out, not_4_out);
  and and_4 (and_4_out, in_3, in_4);
  or or_1 (or_1_out, not_5_out, in_4);
  and and_5 (and_5_out, not_6_out, not_7_out);
  and and_6 (and_6_out, not_8_out, in_3);
  not not_21 (not_21_out, in_4);
  and and_7 (and_7_out, in_2, not_9_out);
  and and_8 (and_8_out, not_10_out, not_11_out);
  and and_9 (and_9_out, in_3, not_12_out);
  and and_10 (and_10_out, not_13_out, not_14_out);
  and and_11 (and_11_out, in_2, not_15_out);
  and and_12 (and_12_out, in_2, not_16_out);
  and and_13 (and_13_out, not_17_out, in_3);
  and and_14 (and_14_out, in_2, not_18_out);
  and and_15 (and_15_out, in_2, not_19_out);
  or or_2 (out_5, and_1_out, in_3, and_2_out, in_1);
  or or_3 (out_6, not_20_out, and_3_out, and_4_out);
  or or_4 (out_7, or_1_out, in_2);
  or or_5 (or_5_out, and_5_out, and_6_out);
  and and_16 (and_16_out, in_3, not_21_out);
  and and_17 (and_17_out, and_7_out, in_4);
  or or_6 (out_9, and_8_out, and_9_out);
  or or_7 (or_7_out, and_10_out, and_11_out);
  or or_8 (or_8_out, and_12_out, in_1);
  or or_9 (or_9_out, and_13_out, and_14_out);
  or or_10 (or_10_out, and_15_out, in_1);
  or or_11 (or_11_out, or_5_out, and_16_out);
  or or_12 (or_12_out, and_17_out, in_1);
  or or_13 (out_10, or_7_out, or_8_out);
  or or_14 (out_11, or_9_out, or_10_out);
  or or_15 (out_8, or_11_out, or_12_out);
endmodule
